# Fritzing sketch Untitled Sketch (saved by Fritzing 0.9.3b)

parts:
  T1 = LM35 Temperature Sensor [package="TO92 [THT]"]
  hc-sr1 = hc-sr04
  Componente1 = Arduino Leonardo (Rev3b)
  LCD1 = LCD screen
  S2 = Momentary Switch [package=ksa_sealed_tac_switch]
  R2 = Resistor [tolerance=±5% resistance=220 package="0805 [SMD]"]
  R3 = Resistor [tolerance=±5% resistance=220 package="0805 [SMD]"]

nets:
  VCC: T1.+Vs, hc-sr1.VCC, Componente1.5V, LCD1.VDD, LCD1.LED+, S2.3
  N1: T1.Vout, Componente1.A0
  GND: T1.GND, hc-sr1.GND, Componente1.GND, LCD1.VSS, LCD1.V0, LCD1.LED-, R2.Pin_0, R3.Pin_1
  N2: hc-sr1.Trig, Componente1.D12/A11
  N3: hc-sr1.Echo, Componente1.D11_PWM
  N4: Componente1.D2/SDA, S2.2, R3.Pin_0
  N5: Componente1.D3_PWM/SCL, LCD1.DB7
  N6: Componente1.D4/A6, LCD1.DB6
  N7: Componente1.D5_PWM, LCD1.DB5
  N8: Componente1.D6_PWM/A7, LCD1.DB4
  N9: Componente1.D7, LCD1.E
  N10: Componente1.D8/A8, LCD1.RS
  N11: LCD1.R/W, R2.Pin_1
